// Logisim project logisim.circ as structural Verilog: 5 circuits, main circuit main
module main (
  input  Cin,
  input  D0,
  input  D1,
  input  in_4,
  input  [3:0] A,
  input  [1:0] in_6,
  input  D2,
  input  [3:0] B,
  input  D3,
  input  CLK,
  input  Cin_2,
  input  [3:0] A_2,
  input  D,
  input  [3:0] B_2,
  output out_15,
  output [3:0] S,
  output out_17,
  output Cout,
  output Q,
  output [3:0] S_2,
  output Q_prime,
  output Cout_2
);

  wire adder_2_cout, adder_3_cout, adder_4_cout, and_1_out, and_2_out, multiplexer_2_out, multiplexer_3_out,
       multiplexer_4_out, not_1_out;

  Multiplexer #(.select(2)) multiplexer_1 (.in0(D0), .in1(D1), .in2(D2), .in3(D3), .out(out_15), .sel(in_6), .en(in_4));
  Multiplexer #(.enable("false")) multiplexer_2 (.in0(D0), .in1(D1), .out(multiplexer_2_out), .sel(in_6[0]));
  Multiplexer #(.enable("false")) multiplexer_3 (.in0(D2), .in1(D3), .out(multiplexer_3_out), .sel(in_6[0]));
  Multiplexer #(.enable("false")) multiplexer_4 (
    .in0(multiplexer_2_out), .in1(multiplexer_3_out), .out(multiplexer_4_out), .sel(in_6[1]));
  Adder #(.width(4)) adder_1 (.a(A_2), .b(B_2), .out(S_2), .cin(Cin_2), .cout(Cout_2));
  xor xor_1 (out_17, out_15, multiplexer_4_out);
  not not_1 (not_1_out, D);
  and and_1 (and_1_out, CLK, not_1_out);
  and and_2 (and_2_out, CLK, D);
  Adder #(.width(1)) adder_2 (.a(A[0]), .b(B[0]), .out(S[0]), .cin(Cin), .cout(adder_2_cout));
  Adder #(.width(1)) adder_3 (.a(A[1]), .b(B[1]), .out(S[1]), .cin(adder_2_cout), .cout(adder_3_cout));
  Adder #(.width(1)) adder_4 (.a(A[2]), .b(B[2]), .out(S[2]), .cin(adder_3_cout), .cout(adder_4_cout));
  Adder #(.width(1)) adder_5 (.a(B[3]), .b(A[3]), .out(S[3]), .cin(adder_4_cout), .cout(Cout));
  nor nor_1 (Q, and_1_out, Q_prime);
  nor nor_2 (Q_prime, and_2_out, Q);
endmodule

module D_latch (
  input  CLK,
  input  D,
  output Q,
  output Q_prime
);

  wire and_1_out, and_2_out, not_1_out;

  not not_1 (not_1_out, D);
  and and_1 (and_1_out, CLK, not_1_out);
  and and_2 (and_2_out, CLK, D);
  nor nor_1 (Q, and_1_out, Q_prime);
  nor nor_2 (Q_prime, and_2_out, Q);
endmodule

module D_Flip_Flop (
  input  CLK,
  input  D,
  output Q,
  output Q_prime
);

  wire d_latch_1_q, not_1_out;

  not not_1 (not_1_out, CLK);
  D_latch d_latch_1 (.CLK(not_1_out), .D(D), .Q(d_latch_1_q));  // open: Q_prime
  D_latch d_latch_2 (.CLK(CLK), .D(d_latch_1_q), .Q(Q), .Q_prime(Q_prime));
endmodule

module _4_bit_register (
  input  CLK,
  input  [3:0] X,
  output [3:0] Y
);

  D_Flip_Flop d_ff_1 (.D(X[0]), .CLK(CLK), .Q(Y[0]));  // open: Q_prime
  D_Flip_Flop d_ff_2 (.D(X[1]), .CLK(CLK), .Q(Y[1]));  // open: Q_prime
  D_Flip_Flop d_ff_3 (.D(X[2]), .CLK(CLK), .Q(Y[2]));  // open: Q_prime
  D_Flip_Flop d_ff_4 (.D(X[3]), .CLK(CLK), .Q(Y[3]));  // open: Q_prime
endmodule

module Sync_Seq_Circ (
  input  [7:0] I,
  input  [7:0] I_2,
  output [7:0] O,
  output [7:0] O_2
);

  wire button_1_out, button_2_out, clock_1_out, clock_2_out;
  wire [7:0] adder_1_out, multiplexer_1_out, not_1_out, not_2_out, register_1_q, register_2_q;

  Register register_1 (.D(adder_1_out), .Q(register_1_q), .clk(clock_1_out));  // open: en, clr
  Clock clock_1 (.out(clock_1_out));
  assign not_1_out = ~I_2;  // NOT_Gate not_1, 8 bits wide
  Register register_2 (.D(O_2), .Q(register_2_q), .clk(clock_2_out));  // open: en, clr
  Clock clock_2 (.out(clock_2_out));
  Multiplexer #(.width(8)) multiplexer_1 (
    .in0(I_2), .in1(not_1_out), .out(multiplexer_1_out), .sel(button_1_out));  // open: en
  Button button_1 (.out(button_1_out));
  Adder adder_1 (.a(I), .b(register_1_q), .out(adder_1_out));  // open: cin, cout
  Adder adder_2 (.a(multiplexer_1_out), .b(register_2_q), .out(O_2), .cin(button_1_out));  // open: cout
  Multiplexer #(.width(8)) multiplexer_2 (.in0(adder_1_out), .in1(not_2_out), .out(O), .sel(button_2_out));  // open: en
  assign not_2_out = ~adder_1_out;  // NOT_Gate not_2, 8 bits wide
  Button button_2 (.out(button_2_out));
endmodule
